# Fritzing sketch lesson10-circuit (saved by Fritzing 0.8.7b)
breadboards: 1

parts:
  LED6 = LED - 5mm [color="Red (633nm)" package="5 mm [THT]"]
  LED7 = LED - 5mm [color="Yellow (595nm)" package="5 mm [THT]"]
  LED8 = LED - 5mm [color="Green (565nm)" package="5 mm [THT]"]
  元件1 = Arduino Uno (Rev3)
  R1 = Resistor [tolerance=±5% resistance=220 package=THT]
  R2 = Resistor [tolerance=±5% resistance=220 package=THT]
  R3 = Resistor [tolerance=±5% resistance=220 package=THT]
  S1 = Pushbutton [package="[THT]"]
  S2 = Pushbutton [package="[THT]"]
  R4 = Resistor [tolerance=±5% resistance=220 package=THT]
  R5 = Resistor [tolerance=±5% resistance=220 package=THT]
  S3 = Pushbutton [package="[THT]"]
  R6 = Resistor [tolerance=±5% resistance=220 package=THT]

nets:
  N1: LED6.cathode, 元件1.D10_PWM/SS
  N2: LED6.anode, R1.Pin_0
  N3: LED7.cathode, 元件1.D9_PWM
  N4: LED7.anode, R2.Pin_0
  N5: LED8.cathode, 元件1.D8
  N6: LED8.anode, R3.Pin_0
  N7: 元件1.D5_PWM, S3.Pin_1, S3.Pin_2, R6.Pin_0
  N8: 元件1.D6_PWM, S2.Pin_1, S2.Pin_2, R5.Pin_0
  N9: 元件1.D7, S1.Pin_1, S1.Pin_2, R4.Pin_0
  N10: R1.Pin_1, R2.Pin_1, R3.Pin_1, R4.Pin_1, R5.Pin_1, R6.Pin_1
  N11: S1.Pin_3, S1.Pin_4, S2.Pin_3, S2.Pin_4, S3.Pin_3, S3.Pin_4
