# Fritzing sketch lesson11-circuit (saved by Fritzing 0.8.7b)
breadboards: 1

parts:
  元件1 = Arduino Uno (Rev3)
  R1 = Rotary Potentiometer (Large) [maximum_resistance=100kΩ package=THT]

nets:
  N1: 元件1.A0, R1.wiper
  N2: 元件1.5V, R1.leg1
  N3: 元件1.GND, R1.leg2
