# Fritzing sketch lesson12-1-circuit (saved by Fritzing 0.8.7b)
breadboards: 1

parts:
  元件1 = Arduino Uno (Rev3)
  R1 = Photocell (LDR) [package=THT]
  J1 = Piezo Speaker

nets:
  N1: 元件1.D6_PWM, R1.pin_1
  N2: 元件1.GND, J1.pin1
  N3: R1.pin_0, J1.pin2
