# Fritzing sketch lesson12-2-circuit (saved by Fritzing 0.8.7b)
breadboards: 1

parts:
  元件1 = Arduino Uno (Rev3)
  LED1 = LED - 5mm [color="Red (633nm)" package="5 mm [THT]"]
  R1 = Photocell (LDR) [package=THT]
  R2 = Resistor [tolerance=±5% resistance=220 package=THT]

nets:
  N1: 元件1.A0, R2.Pin_1
  N2: 元件1.D11_PWM/MOSI, LED1.cathode
  N3: 元件1.5V, R1.pin_0
  N4: 元件1.GND, LED1.anode, R1.pin_1, R2.Pin_0
