# Fritzing sketch lesson13-circuit (saved by Fritzing 0.8.7b)
breadboards: 1

parts:
  LED1 = smd LED [color="Red (660nm)" package="0603 [SMD]"]
  元件1 = Arduino Uno (Rev3)
  J1 = Piezo Speaker
  R1 = Resistor [tolerance=±5% resistance=10k package=THT]

nets:
  N1: LED1.cathode, 元件1.5V
  N2: LED1.anode, 元件1.A5/SCL, R1.Pin_0
  N3: 元件1.D8, J1.pin2
  N4: 元件1.GND, J1.pin1, R1.Pin_1

notes:
  Fire Sensor
