# Fritzing sketch lesson14-circuit (saved by Fritzing 0.8.7b)
breadboards: 1

parts:
  元件1 = Arduino Uno (Rev3)
  R1 = Resistor [tolerance=±5% resistance=1k package=THT]
  BAT1 = Battery Holders [package=battery-aa]

nets:
  N1: 元件1.A0, R1.Pin_1
  N2: 元件1.GND, R1.Pin_0, BAT1.+
