# Fritzing sketch lesson15-circuit (saved by Fritzing 0.8.7b)
breadboards: 1

parts:
  元件1 = Arduino Uno (Rev3)
  T1 = LM35 Temperature Sensor [package="TO92 [THT]"]

nets:
  N1: 元件1.A0, T1.Vout
  N2: 元件1.5V, T1.+Vs
  GND: 元件1.GND, T1.GND
