# Fritzing sketch lesson16-circuit (saved by Fritzing 0.8.7b)
breadboards: 1

parts:
  元件2 = Arduino Uno (Rev3)
  LED9 = LED - 5mm [color="Red (633nm)" package="5 mm [THT]"]  # not connected
  LED10 = LED - 5mm [color="Yellow (595nm)" package="5 mm [THT]"]
  LED11 = LED - 5mm [color="Green (565nm)" package="5 mm [THT]"]  # not connected
  R4 = Resistor [tolerance=±5% resistance=220 package=THT]
  R5 = Resistor [tolerance=±5% resistance=220 package=THT]
  R6 = Resistor [tolerance=±5% resistance=220 package=THT]
  T1 = LM35 Temperature Sensor [package="TO92 [THT]"]

nets:
  N1: 元件2.A0, T1.Vout
  N2: 元件2.D12/MISO, LED10.cathode
  GND: 元件2.GND, R4.Pin_1, R5.Pin_1, R6.Pin_1, T1.GND
  N3: 元件2.5V, T1.+Vs
  N4: LED10.anode, R5.Pin_0
