# Fritzing sketch lesson17-circuit (saved by Fritzing 0.8.7b)
breadboards: 1

parts:
  元件1 = Arduino Uno (Rev3)
  DI1 = 7-Segment LED Display [package=THT]

nets:
  N1: 元件1.D8, DI1.cathodeG
  N2: 元件1.D9_PWM, DI1.cathodeDP
  N3: 元件1.GND, DI1.commAnode
  N4: 元件1.D2, DI1.cathodeA
  N5: 元件1.D3_PWM, DI1.cathodeB
  N6: 元件1.D4, DI1.cathodeC
  N7: 元件1.D5_PWM, DI1.cathodeD
  N8: 元件1.D6_PWM, DI1.cathodeE
  N9: 元件1.D7, DI1.cathodeF
