# Fritzing sketch lesson18-circuit (saved by Fritzing 0.8.7b)
breadboards: 1

parts:
  7_Segment_4_Digit_Display2 = 7-SEGMENT-4DIGIT common anode [part_number="5461BS - 5462BS" package=7-segment-4digit-anode]
  元件1 = Arduino Uno (Rev3)

nets:
  N1: 7_Segment_4_Digit_Display2.pin_2, 元件1.D6_PWM
  N2: 7_Segment_4_Digit_Display2.pin_3, 元件1.D5_PWM
  N3: 7_Segment_4_Digit_Display2.pin_4, 元件1.D4
  N4: 7_Segment_4_Digit_Display2.pin_5, 元件1.D3_PWM
  N5: 7_Segment_4_Digit_Display2.pin_6, 元件1.D2
  N6: 7_Segment_4_Digit_Display2.pin_7, 元件1.D8
  N7: 7_Segment_4_Digit_Display2.pin_8, 元件1.D9_PWM
  N8: 7_Segment_4_Digit_Display2.pin_9, 元件1.D10_PWM/SS
  N9: 7_Segment_4_Digit_Display2.pin_10, 元件1.D11_PWM/MOSI
  N10: 7_Segment_4_Digit_Display2.pin_11, 元件1.D12/MISO
  N11: 7_Segment_4_Digit_Display2.pin_12, 元件1.D13/SCK

custom parts:
  7-SEGMENT-4DIGIT common anode: A 7 Segment 4 Digit common anode display, with decimal points
