# Fritzing sketch lesson19-circuit (saved by Fritzing 0.8.7b)

parts:
  8x8_LED_matrix_MAX1 = 8x8 Red 8x8 LED Matrix with MAX7219
  元件1 = Arduino Uno (Rev3)

nets:
  VCC: 8x8_LED_matrix_MAX1.VCC, 8x8_LED_matrix_MAX1.VCC_PT, 元件1.5V
  GND: 8x8_LED_matrix_MAX1.GND, 8x8_LED_matrix_MAX1.CLK_PT, 元件1.GND
  N1: 8x8_LED_matrix_MAX1.GND_PT, 8x8_LED_matrix_MAX1.CLK, 元件1.D11_PWM/MOSI
  N2: 8x8_LED_matrix_MAX1.DIN, 元件1.D12/MISO
  N3: 8x8_LED_matrix_MAX1.DIN_CHN, 8x8_LED_matrix_MAX1.CS, 元件1.D10_PWM/SS

custom parts:
  8x8 Red 8x8 LED Matrix with MAX7219: Description: 8 by 8 red LED matrix with a MAX7219 controller.
