# Fritzing sketch lesson2-circuit (saved by Fritzing 0.8.7b)
breadboards: 1

parts:
  元件1 = Arduino Uno (Rev3)
  LED1 = LED - 5mm [color="Red (633nm)" package="5 mm [THT]"]

nets:
  N1: 元件1.D13/SCK, LED1.cathode
  N2: 元件1.GND, LED1.anode
