# Fritzing sketch lesson20-circuit (saved by Fritzing 0.8.7b)
breadboards: 1

parts:
  LED2 = RGB LED (com. anode, rbg) [package="5 mm [THT]"]
  元件1 = Arduino Uno (Rev3)

nets:
  N1: LED2.red_cathode, 元件1.D11_PWM/MOSI
  N2: LED2.common_anode, 元件1.5V
  N3: LED2.blue_cathode, 元件1.D10_PWM/SS
  N4: LED2.green_cathode, 元件1.D9_PWM
