# Fritzing sketch lesson21-circuit (saved by Fritzing 0.8.7b)
breadboards: 1

parts:
  U1 = 74HC595 SMD [package="SO16 [SMD]"]
  元件1 = Arduino Uno (Rev3)
  LED1 = LED - 5mm [color="Red (633nm)" package="5 mm [THT]"]
  LED2 = LED - 5mm [color="Red (633nm)" package="5 mm [THT]"]
  LED3 = LED - 5mm [color="Red (633nm)" package="5 mm [THT]"]
  LED4 = LED - 5mm [color="Red (633nm)" package="5 mm [THT]"]
  LED5 = LED - 5mm [color="Red (633nm)" package="5 mm [THT]"]
  LED6 = LED - 5mm [color="Red (633nm)" package="5 mm [THT]"]
  LED7 = LED - 5mm [color="Red (633nm)" package="5 mm [THT]"]
  LED8 = LED - 5mm [color="Red (633nm)" package="5 mm [THT]"]

nets:
  N1: U1.Q1, LED1.cathode
  N2: U1.Q2, LED3.cathode
  N3: U1.Q3, LED4.cathode
  N4: U1.Q4, LED6.cathode
  N5: U1.Q6, LED5.cathode
  N6: U1.Q7, LED8.cathode
  N7: U1.GND, LED1.anode, LED2.anode, LED3.anode, LED4.anode, LED5.anode, LED6.anode, LED7.anode, LED8.anode
  N8: U1.MR, U1.VCC
  N9: U1.SH_CP, 元件1.D5_PWM
  N10: U1.ST_CP, 元件1.D4
  N11: U1.DS, 元件1.D2
  N12: U1.Q0, LED2.cathode
