# Fritzing sketch lesson22-1-circuit (saved by Fritzing 0.8.7b)

parts:
  元件2 = Arduino Uno (Rev3)
  Keypad4x2 = Keypad Membran 4x4
  LED1 = LED - 5mm [color="Red (633nm)" package="5 mm [THT]"]

nets:
  N1: 元件2.D8, Keypad4x2.Pin6
  N2: 元件2.D9_PWM, Keypad4x2.Pin5
  N3: 元件2.D10_PWM/SS, Keypad4x2.Pin4
  N4: 元件2.D11_PWM/MOSI, Keypad4x2.Pin3
  N5: 元件2.D12/MISO, Keypad4x2.Pin2
  N6: 元件2.D13/SCK, Keypad4x2.Pin1
  N7: 元件2.GND, LED1.anode
  N8: 元件2.D2, LED1.cathode
  N9: 元件2.D6_PWM, Keypad4x2.Pin8
  N10: 元件2.D7, Keypad4x2.Pin7

custom parts:
  Keypad Membran 4x4: Membrane Keypad 4x4 Matrix
