# Fritzing sketch lesson22-2-circuit (saved by Fritzing 0.8.7b)

parts:
  Keypad4x1 = Keypad Membran 4x4
  元件1 = Arduino Uno (Rev3)

nets:
  N1: Keypad4x1.Pin1, 元件1.D13/SCK
  N2: Keypad4x1.Pin2, 元件1.D12/MISO
  N3: Keypad4x1.Pin3, 元件1.D11_PWM/MOSI
  N4: Keypad4x1.Pin4, 元件1.D10_PWM/SS
  N5: Keypad4x1.Pin5, 元件1.D9_PWM
  N6: Keypad4x1.Pin6, 元件1.D8
  N7: Keypad4x1.Pin7, 元件1.D7
  N8: Keypad4x1.Pin8, 元件1.D6_PWM

custom parts:
  Keypad Membran 4x4: Membrane Keypad 4x4 Matrix
