# Fritzing sketch lesson23-circuit (saved by Fritzing 0.8.7b)
breadboards: 1

parts:
  M1 = DC Motor
  元件1 = Arduino Uno (Rev3)
  Q1 = NPN-Transistor [package="TO92 [THT]"]
  R1 = Resistor [tolerance=±5% resistance=330 package=THT]
  D1 = Rectifier Diode [part_number=1N4001 package="300 mil [THT]"]

nets:
  N1: M1.pin_1, Q1.C, D1.anode
  N2: M1.pin_2, 元件1.5V, D1.cathode
  N3: 元件1.GND, Q1.E
  N4: 元件1.D3_PWM, R1.Pin_0
  N5: Q1.B, R1.Pin_1

notes:
  PN2222
  1N4001
