# Fritzing sketch lesson24-circuit (saved by Fritzing 0.8.7b)

parts:
  Water_Level_Sensor1 = Water Level Sensor
  LED1 = LED - 5mm [color="Red (633nm)" package="5 mm [THT]"]
  元件1 = Arduino Uno (Rev3)

nets:
  N1: Water_Level_Sensor1.SIG, 元件1.A0
  VCC: Water_Level_Sensor1.VCC, 元件1.5V
  GND: Water_Level_Sensor1.GND, LED1.anode, 元件1.GND
  N2: LED1.cathode, 元件1.D2

custom parts:
  Water Level Sensor: A water level sensor. This sensor operates at 3V to 5V. The Sig (signal) pin outputs an analogue signal that is in proportion to the amount of water in contact with the sensor.
