# Fritzing sketch lesson25-circuit (saved by Fritzing 0.8.7b)

parts:
  元件1 = SRF05 Ultrasonic Rangefinder
  元件2 = Arduino Uno (Rev3)

nets:
  VCC: 元件1.VCC, 元件2.5V
  N1: 元件1.Trig, 元件2.D4
  N2: 元件1.Echo, 元件2.D5_PWM
  GND: 元件1.GND, 元件2.GND
