# Fritzing sketch lesson26-circuit (saved by Fritzing 0.8.7b)

parts:
  KY-7 = Keyes Relay [package=THT]
  元件1 = Arduino Uno (Rev3)

nets:
  N1: KY-7.signal, 元件1.D2
  N2: KY-7.power, 元件1.5V
  N3: KY-7.ground, 元件1.GND

custom parts:
  Keyes Relay: The Keyes 5V relay module is suitable for SCM development, home appliance control. It uses a 5V~12V TIL control signal which can control DC / AC signal.
