# Fritzing sketch lesson28-circuit (saved by Fritzing 0.8.7b)

parts:
  X2 = X113647 Stepper Driver Board [package=board]
  MOTOR2 = 28BYJ-48 Stepper Motor
  元件1 = Arduino Uno (Rev3)

nets:
  N1: X2.IN1, 元件1.D8
  N2: X2.IN2, 元件1.D9_PWM
  N3: X2.IN3, 元件1.D10_PWM/SS
  N4: X2.IN4, 元件1.D11_PWM/MOSI
  GND: X2.GND, 元件1.GND
  N5: X2.+V, 元件1.5V
  N6: X2.BLUE, MOTOR2.BLUE
  N7: X2.PINK, MOTOR2.PINK
  N8: X2.YELLOW, MOTOR2.YELLOW
  N9: X2.ORANGE, MOTOR2.ORANGE
  N10: X2.RED, MOTOR2.RED

custom parts:
  X113647 Stepper Driver Board: A common stepper motor driver board based on ULN2003APG darlington array
  28BYJ-48 Stepper Motor: 28BYJ-48 gear-reduction stepper motor (small)
