# Fritzing sketch lesson3-circuit (saved by Fritzing 0.8.7b)
breadboards: 1

parts:
  R1 = Resistor [tolerance=±5% resistance=220 package=THT]
  元件1 = Arduino Uno (Rev3)
  R2 = Rotary Potentiometer (Large) [maximum_resistance=100kΩ package=THT]
  LED1 = LED - 5mm [color="Red (633nm)" package="5 mm [THT]"]

nets:
  N1: R1.Pin_0, LED1.anode
  N2: R1.Pin_1, 元件1.GND, R2.leg2
  N3: 元件1.A0, R2.wiper
  N4: 元件1.D11_PWM/MOSI, LED1.cathode
  N5: 元件1.5V, R2.leg1
