# Fritzing sketch lesson30-circuit (saved by Fritzing 0.8.7b)

parts:
  元件1 = Thumb Joystick
  元件2 = Arduino Uno (Rev3)

nets:
  GND: 元件1.GND, 元件2.GND
  N1: 元件1.SEL, 元件2.D7
  N2: 元件1.HORZ, 元件2.A0
  N3: 元件1.VERT, 元件2.A1
  VCC: 元件1.VCC, 元件2.5V
