# Fritzing sketch lesson31-circuit (saved by Fritzing 0.8.7b)

parts:
  元件1 = IR Receiver Breakout [package=PCB]
  元件2 = Arduino Uno (Rev3)

nets:
  GND: 元件1.GND, 元件2.GND
  N1: 元件1.OUT, 元件2.5V
  N2: 元件1.VCC, 元件2.D2
