# Fritzing sketch lesson33-circuit (saved by Fritzing 0.8.7b)

parts:
  元件1 = RFID-RC522-v2
  元件2 = Arduino Uno (Rev3)

nets:
  N1: 元件1.SCK, 元件2.D10_PWM/SS
  N2: 元件1.MOSI, 元件2.D13/SCK
  N3: 元件1.MISO, 元件2.D11_PWM/MOSI
  N4: 元件1.IRQ, 元件2.D12/MISO
  GND: 元件1.GND, 元件2.GND
  N5: 元件1.RST, 元件2.A0
  3.3V: 元件1.3.3V, 元件2.5V

custom parts:
  RFID-RC522-v2: A simple China made RFID-RC522 Reader; do check the pin labels, as this is a MFRC522 based clone.
