# Fritzing sketch lesson4-circuit (saved by Fritzing 0.8.7b)
breadboards: 1

parts:
  元件1 = Arduino Uno (Rev3)
  LED1 = LED - 5mm [color="Red (633nm)" package="5 mm [THT]"]
  R1 = Resistor [tolerance=±5% resistance=220 package=THT]

nets:
  N1: 元件1.D10_PWM/SS, LED1.cathode
  N2: 元件1.GND, R1.Pin_1
  N3: LED1.anode, R1.Pin_0
