# Fritzing sketch lesson6-circuit (saved by Fritzing 0.8.7b)
breadboards: 1

parts:
  元件1 = Arduino Uno (Rev3)
  LED3 = LED - 5mm [color="Yellow (595nm)" package="5 mm [THT]"]
  LED4 = LED - 5mm [color="Red (633nm)" package="5 mm [THT]"]
  LED5 = LED - 5mm [color="Green (565nm)" package="5 mm [THT]"]
  R1 = Resistor [tolerance=±5% resistance=220 package=THT]
  R2 = Resistor [tolerance=±5% resistance=220 package=THT]
  R3 = Resistor [tolerance=±5% resistance=220 package=THT]

nets:
  N1: 元件1.GND, R1.Pin_1, R2.Pin_1, R3.Pin_1
  N2: 元件1.D3_PWM, LED4.cathode
  N3: 元件1.D5_PWM, LED3.cathode
  N4: 元件1.D7, LED5.cathode
  N5: LED3.anode, R2.Pin_0
  N6: LED4.anode, R1.Pin_0
  N7: LED5.anode, R3.Pin_0
