# Fritzing sketch lesson8-circuit (saved by Fritzing 0.8.7b)
breadboards: 1

parts:
  S2 = Tilt Switch [package=THT]
  元件1 = Arduino Uno (Rev3)
  LED1 = LED - 5mm [color="Red (633nm)" package="5 mm [THT]"]
  R1 = Resistor [tolerance=±5% resistance=220 package=THT]

nets:
  N1: S2.Pin_1, 元件1.5V
  N2: S2.Pin_2, 元件1.A5/SCL, R1.Pin_0
  N3: 元件1.D8, LED1.cathode
  N4: 元件1.GND, LED1.anode, R1.Pin_1
