# Fritzing sketch lesson9-circuit (saved by Fritzing 0.8.7b)
breadboards: 1

parts:
  元件1 = Arduino Uno (Rev3)
  S1 = Pushbutton [package="[THT]"]
  LED1 = LED - 5mm [color="Red (633nm)" package="5 mm [THT]"]
  R1 = Resistor [tolerance=±5% resistance=220 package=THT]
  R2 = Resistor [tolerance=±5% resistance=220 package=THT]

nets:
  N1: 元件1.D11_PWM/MOSI, LED1.cathode
  N2: 元件1.D7, S1.Pin_1, S1.Pin_2, R2.Pin_0
  N3: 元件1.5V, S1.Pin_3, S1.Pin_4
  N4: 元件1.GND, R1.Pin_1, R2.Pin_1
  N5: LED1.anode, R1.Pin_0
